# Fritzing sketch thebaud-thomas-assignment-2 (saved by Fritzing 0.9.3b)
breadboards: 1

parts:
  S1 = Pushbutton [package="[THT]"]
  S2 = Pushbutton [package="[THT]"]
  S3 = Pushbutton [package="[THT]"]
  S4 = Pushbutton [package="[THT]"]
  R1 = Resistor [tolerance=±5% resistance=220 package=THT]
  R2 = Resistor [tolerance=±5% resistance=220 package=THT]
  R3 = Resistor [tolerance=±5% resistance=220 package=THT]
  R4 = Resistor [tolerance=±5% resistance=220 package=THT]
  LED1 = smd LED [color="Red (633nm)" package="1206 [SMD]"]
  LED2 = smd LED [color="Red (633nm)" package="1206 [SMD]"]
  LED3 = smd LED [color="Red (633nm)" package="1206 [SMD]"]
  LED4 = smd LED [color="Red (633nm)" package="1206 [SMD]"]
  D1 = Schottky Diode [part_number=1N5817 package="Melf DO-213 AB [SMD]"]
  D2 = Schottky Diode [part_number=1N5817 package="Melf DO-213 AB [SMD]"]
  D3 = Schottky Diode [part_number=1N5817 package="Melf DO-213 AB [SMD]"]
  D4 = Schottky Diode [part_number=1N5817 package="Melf DO-213 AB [SMD]"]
  Part1 = Arduino Uno (Rev3) - ICSP
  R6 = Trimmer Potentiometer [maximum_resistance=10kΩ package=THT]
  J1 = Piezo Speaker
  LCD1 = LCD screen
  R7 = Resistor [tolerance=±5% resistance=220 package="0402 [SMD]"]

nets:
  GND: S1.Pin_1, S1.Pin_2, S2.Pin_1, S2.Pin_2, S3.Pin_1, S3.Pin_2, S4.Pin_1, S4.Pin_2, Part1.GND, R6.leg2, LCD1.VSS, LCD1.R/W, LCD1.LED-
  N1: S1.Pin_3, S1.Pin_4, LED1.cathode, D1.anode
  N2: S2.Pin_3, S2.Pin_4, LED2.cathode, D2.anode
  N3: S3.Pin_3, S3.Pin_4, LED3.cathode, D3.anode
  N4: S4.Pin_3, S4.Pin_4, LED4.cathode, D4.anode
  5V: R1.Pin_0, R2.Pin_0, R3.Pin_0, R4.Pin_0, Part1.5V, R6.leg1, J1.pin2, LCD1.VDD, R7.Pin_1
  N5: R1.Pin_1, LED1.anode
  N6: R2.Pin_1, LED4.anode
  N7: R3.Pin_1, LED3.anode
  N8: R4.Pin_1, LED2.anode
  N9: D1.cathode, Part1.D3_PWM
  N10: D2.cathode, Part1.D4
  N11: D3.cathode, Part1.D5_PWM
  N12: D4.cathode, Part1.D6_PWM
  N13: Part1.ICSP_MISO, Part1.D12/MISO, LCD1.RS
  N14: Part1.ICSP_MOSI, Part1.D11_PWM/MOSI, LCD1.E
  N15: Part1.D8, LCD1.DB6
  N16: Part1.D9_PWM, LCD1.DB5
  N17: Part1.D10_PWM/SS, LCD1.DB4
  N18: Part1.D2, J1.pin1
  N19: Part1.D7, LCD1.DB7
  N20: R6.wiper, LCD1.V0
  N21: LCD1.LED+, R7.Pin_0
